# Fritzing sketch Rpi2GPIO (saved by Fritzing 0.9.2b)
breadboards: 1

parts:
  Raspberry_Pi_2 = Raspberry Pi 2
  DHT11 = Humidity and Temperature Sensor RHT03
  R1 = Resistor [tolerance=±5% resistance=220 package=THT]
  R2 = Resistor [tolerance=±5% resistance=220 package=THT]

nets:
  3V3: Raspberry_Pi_2.3v3, Raspberry_Pi_2.3V3, DHT11.Vcc, R1.Pin_0
  N1: Raspberry_Pi_2.GND, DHT11.GND_2
  N2: Raspberry_Pi_2.GPIO23, DHT11.Data-signal, R2.Pin_1
  N3: R1.Pin_1, R2.Pin_0
